// Logisim project decoder_.circ as structural Verilog: 1 circuit, main circuit main
module main (
  input  x0,
  input  x1,
  input  E,
  output [3:0] dataOut
);

  and and_1 (dataOut[3], ~x0, ~x1, E);  // AND_Gate
  and and_2 (dataOut[2], ~x0, x1, E);  // AND_Gate
  and and_3 (dataOut[1], x0, ~x1, E);  // AND_Gate
  and and_4 (dataOut[0], x0, x1, E);

  // Notes on the sheet:
  //   Decoder
endmodule
