// Logisim project encoder.circ as structural Verilog: 1 circuit, main circuit main
module main (
  input  x0,
  input  x1,
  input  x2,
  input  x3,
  output [1:0] dataOut
);

  wire and_1_out, and_2_out, and_3_out, and_4_out;

  and and_1 (and_1_out, ~x0, ~x1, x2);  // AND_Gate
  and and_2 (and_2_out, ~x0, ~x1, ~x2, x3);  // AND_Gate
  and and_3 (and_3_out, ~x0, x1);  // AND_Gate
  and and_4 (and_4_out, ~x0, ~x1, ~x2, x3);  // AND_Gate
  or or_1 (dataOut[1], and_1_out, and_2_out);
  or or_2 (dataOut[0], and_3_out, and_4_out);

  // Notes on the sheet:
  //   Encoder
endmodule
