// Logisim project flipflop.circ as structural Verilog: 1 circuit, main circuit main
module main (
  input  DataIn,
  input  Clock,
  output Q,
  output nQ
);

  wire nand_1_out, nand_2_out;

  nand nand_1 (nand_1_out, DataIn, Clock);
  nand nand_2 (nand_2_out, Clock, ~DataIn);  // NAND_Gate
  nand nand_3 (Q, nand_1_out, nQ);
  nand nand_4 (nQ, nand_2_out, Q);
endmodule
