// Logisim project multiplexer.circ as structural Verilog: 1 circuit, main circuit main
module main (
  input  x0,
  input  x1,
  input  x2,
  input  x3,
  input  [1:0] C,
  output out_6
);

  wire and_1_out, and_2_out, and_3_out, and_4_out;

  and and_1 (and_1_out, x0, ~C[1], ~C[0]);  // AND_Gate
  and and_2 (and_2_out, x1, ~C[1], C[0]);  // AND_Gate
  and and_3 (and_3_out, x2, C[1], ~C[0]);  // AND_Gate
  and and_4 (and_4_out, x3, C[1], C[0]);
  or or_1 (out_6, and_1_out, and_2_out, and_3_out, and_4_out);

  // Notes on the sheet:
  //   Multiplexer
endmodule
