// Logisim project sum&sub_with_decimal.circ as structural Verilog: 4 circuits, main circuit main
module main (
  input  [3:0] X,
  input  OP,
  input  [3:0] Y,
  output [3:0] risultato
);

  wire fulladder_1_cn_plus_1, fulladder_2_cn_plus_1, fulladder_3_cn_plus_1;
  wire [3:0] controlled_not_1_dataout;

  controlled_not controlled_not_1 (.DataIn(Y), .OP(OP), .DataOut(controlled_not_1_dataout));
  fullAdder fulladder_1 (
    .Xn(X[0]), .Yn(controlled_not_1_dataout[0]), .Cn(OP), .Sn(risultato[0]), .Cn_plus_1(fulladder_1_cn_plus_1));
  fullAdder fulladder_2 (
    .Xn(X[1]), .Yn(controlled_not_1_dataout[1]), .Cn(fulladder_1_cn_plus_1), .Sn(risultato[1]),
    .Cn_plus_1(fulladder_2_cn_plus_1));
  fullAdder fulladder_3 (
    .Xn(X[2]), .Yn(controlled_not_1_dataout[2]), .Cn(fulladder_2_cn_plus_1), .Sn(risultato[2]),
    .Cn_plus_1(fulladder_3_cn_plus_1));
  fullAdder fulladder_4 (
    .Xn(X[3]), .Yn(controlled_not_1_dataout[3]), .Cn(fulladder_3_cn_plus_1), .Sn(risultato[3]));  // open: Cn_plus_1
endmodule

module HalfAdder (
  input  x,
  input  y,
  output somma,
  output c1
);

  xor xor_1 (somma, x, y);
  and and_1 (c1, x, y);
endmodule

module fullAdder (
  input  Xn,
  input  Yn,
  input  Cn,
  output Sn,
  output Cn_plus_1
);

  wire and_1_out, and_2_out, and_3_out, and_4_out, and_5_out, and_6_out, and_7_out, and_8_out;

  and and_1 (and_1_out, ~Xn, ~Yn, Cn);  // AND_Gate
  and and_2 (and_2_out, ~Xn, Yn, ~Cn);  // AND_Gate
  and and_3 (and_3_out, Xn, ~Yn, ~Cn);  // AND_Gate
  and and_4 (and_4_out, Xn, Yn, Cn);
  and and_5 (and_5_out, ~Xn, Yn, Cn);  // AND_Gate
  and and_6 (and_6_out, Xn, ~Yn, Cn);  // AND_Gate
  and and_7 (and_7_out, Xn, Yn, ~Cn);  // AND_Gate
  and and_8 (and_8_out, Xn, Yn, Cn);
  or or_1 (Sn, and_1_out, and_2_out, and_3_out, and_4_out);
  or or_2 (Cn_plus_1, and_5_out, and_6_out, and_7_out, and_8_out);
endmodule

module controlled_not (
  input  [3:0] DataIn,
  input  OP,
  output [3:0] DataOut
);

  xor xor_1 (DataOut[0], DataIn[0], OP);
  xor xor_2 (DataOut[1], DataIn[1], OP);
  xor xor_3 (DataOut[2], DataIn[2], OP);
  xor xor_4 (DataOut[3], DataIn[3], OP);
endmodule
