// Logisim project sum.circ as structural Verilog: 3 circuits, main circuit main
module main (
  input  [3:0] in_1,
  input  [3:0] in_2,
  output [4:0] risultato
);

  wire binaryadder_1_cn_plus_1, binaryadder_2_cn_plus_1, halfadder_1_c1;

  HalfAdder halfadder_1 (.x(in_1[0]), .y(in_2[0]), .somma(risultato[0]), .c1(halfadder_1_c1));
  binaryAdder binaryadder_1 (
    .Xn(in_1[1]), .Yn(in_2[1]), .Cn(halfadder_1_c1), .Sn(risultato[1]), .Cn_plus_1(binaryadder_1_cn_plus_1));
  binaryAdder binaryadder_2 (
    .Xn(in_1[2]), .Yn(in_2[2]), .Cn(binaryadder_1_cn_plus_1), .Sn(risultato[2]),
    .Cn_plus_1(binaryadder_2_cn_plus_1));
  binaryAdder binaryadder_3 (
    .Xn(in_1[3]), .Yn(in_2[3]), .Cn(binaryadder_2_cn_plus_1), .Sn(risultato[3]), .Cn_plus_1(risultato[4]));
endmodule

module HalfAdder (
  input  x,
  input  y,
  output somma,
  output c1
);

  xor xor_1 (somma, x, y);
  and and_1 (c1, x, y);
endmodule

module binaryAdder (
  input  Xn,
  input  Yn,
  input  Cn,
  output Sn,
  output Cn_plus_1
);

  wire and_1_out, and_2_out, and_3_out, and_4_out, and_5_out, and_6_out, and_7_out, and_8_out;

  and and_1 (and_1_out, ~Xn, ~Yn, Cn);  // AND_Gate
  and and_2 (and_2_out, ~Xn, Yn, ~Cn);  // AND_Gate
  and and_3 (and_3_out, Xn, ~Yn, ~Cn);  // AND_Gate
  and and_4 (and_4_out, Xn, Yn, Cn);
  and and_5 (and_5_out, ~Xn, Yn, Cn);  // AND_Gate
  and and_6 (and_6_out, Xn, ~Yn, Cn);  // AND_Gate
  and and_7 (and_7_out, Xn, Yn, ~Cn);  // AND_Gate
  and and_8 (and_8_out, Xn, Yn, Cn);
  or or_1 (Sn, and_1_out, and_2_out, and_3_out, and_4_out);
  or or_2 (Cn_plus_1, and_5_out, and_6_out, and_7_out, and_8_out);
endmodule
